# Fritzing sketch Schematics (saved by Fritzing 0.9.3b)
breadboards: 1

parts:
  R1 = Resistor [tolerance=±5% resistance=680 package=THT]
  U1 = LCD-16X2 [package=lcd-16x2]
  Componente1 = Arduino Pro Mini (5V)
  R2 = Trimmer Potentiometer [maximum_resistance=10kΩ package=THT]
  J1 = Power Jack [package=power_jack_pth_lock]
  JP1 = Header 4 [package=molex-1x4_lock]
  JP2 = Header 4 [package=molex-1x4_lock]
  DS2 = DS18B20 1-Wire Temperature Sensor [part_number=DS18B20]
  DS1 = DS18B20 1-Wire Temperature Sensor [part_number=DS18B20]

nets:
  VDD: R1.Pin_0, U1.VDD, Componente1.VCC, R2.leg2, DS2.VDD, DS1.VDD
  N1: R1.Pin_1, U1.A
  GND: U1.VSS, U1.R_W, U1.K, Componente1.GND, R2.leg1, J1.GND, JP1.1, JP2.1, DS2.GND, DS1.GND
  N2: U1.VO, R2.wiper
  N3: U1.RS, Componente1.MOSI
  N4: U1.E, Componente1.MISO
  N5: U1.DB4, Componente1.A0
  N6: U1.DB5, Componente1.A1
  N7: U1.DB6, Componente1.A2
  N8: U1.DB7, Componente1.A3
  N9: Componente1.RAW, J1.PWR, JP1.2, JP2.2
  N10: Componente1.D9, DS2.DQ, DS1.DQ
  N11: Componente1.D6, JP2.4
  N12: Componente1.D5, JP1.4
  N13: Componente1.D3, JP2.3
  N14: Componente1.D2, JP1.3
